# Fritzing sketch timer_box (saved by Fritzing 0.9.3b)
breadboards: 1

parts:
  Part1 = Arduino Nano (Rev3.0)
  LCD1 = LCD screen  # not connected
  LED1 = LED - 5mm [color="Blue (430nm)" package="5 mm [THT]"]
  R1 = Rotary Potentiometer (Small) [maximum_resistance=100kΩ package=THT]
  J1 = Piezo Speaker
  S1 = Round Pushbutton
  R2 = Resistor [tolerance=±5% resistance=220 package="2010 [SMD]"]
  JP2 = Header 4 [package=screwterminal-3.5mm-4_lock]

nets:
  N1: Part1.GND, LED1.cathode, R1.leg2, J1.pin1, S1.leg0, JP2.4
  N2: Part1.D2, J1.pin2
  N3: Part1.D6, LED1.anode
  N4: Part1.D10, S1.leg1, R2.Pin_0
  N5: Part1.5V, R1.leg1, R2.Pin_1, JP2.3
  N6: Part1.A5, JP2.2
  N7: Part1.A4, JP2.1
  N8: Part1.A2, R1.wiper

notes:
  Display LCD 16×02 (I2C adapter)
  Push Button (Pbs-29)
