# Fritzing sketch timer_box (saved by Fritzing 0.9.3b)
breadboards: 1

parts:
  Part1 = Arduino Nano (Rev3.0)
  LCD1 = LCD screen  # not connected
  LED1 = LED - 5mm [color="Blue (430nm)" package="5 mm [THT]"]
  R1 = Rotary Potentiometer (Small) [maximum_resistance=100kΩ package=THT]
  J1 = Piezo Speaker

nets:
  N1: Part1.GND, LED1.anode, R1.leg2, J1.pin1
  N2: Part1.D2, J1.pin2
  N3: Part1.D4, LED1.cathode
  N4: Part1.5V, R1.leg1
  N5: Part1.A0, R1.wiper
